// Logisim project ALU_kindof.circ as structural Verilog: 1 circuit, main circuit main
module main (
  input  CS,
  input  [1:0] OperationSelect,
  input  [7:0] DATA,
  input  ADR,
  input  RNW,
  output [7:0] CARRY,
  output [7:0] RESULT
);

  wire ADD, COMP, decoder_1_out0, decoder_1_out1, MUL, SUB;
  wire [2:0] controlled_buffer_4_out;
  wire [7:0] A_q, adder_1_out, B_q, multiplier_1_out, subtractor_1_out;
  wire [12:0] CARRY_t;

  Decoder decoder_1 (.out0(decoder_1_out0), .out1(decoder_1_out1), .sel(ADR), .en(CS));
  Decoder #(.select(2)) decoder_2 (.out0(ADD), .out1(SUB), .out2(MUL), .out3(COMP), .sel(OperationSelect), .en(CS));
  Register A (.D(DATA), .en(decoder_1_out0), .clk(RNW), .Q(A_q));  // open: clr
  Register B (.D(DATA), .en(decoder_1_out1), .clk(RNW), .Q(B_q));  // open: clr
  Adder adder_1 (.a(A_q), .b(B_q), .out(adder_1_out), .cout(CARRY_t[0]));  // open: cin
  Subtractor subtractor_1 (.a(A_q), .b(B_q), .out(subtractor_1_out), .bout(CARRY_t[1]));  // open: bin
  Multiplier multiplier_1 (.a(A_q), .b(B_q), .out(multiplier_1_out), .cout(CARRY_t[9:2]));  // open: cin
  Comparator comparator_1 (.a(A_q), .b(B_q), .gt(CARRY_t[10]), .eq(CARRY_t[11]), .lt(CARRY_t[12]));
  assign RESULT = ADD ? adder_1_out : 8'bz;  // Controlled_Buffer controlled_buffer_1
  assign RESULT = SUB ? subtractor_1_out : 8'bz;  // Controlled_Buffer controlled_buffer_2
  assign RESULT = MUL ? multiplier_1_out : 8'bz;  // Controlled_Buffer controlled_buffer_3
  // Probe on CARRY_t
  assign controlled_buffer_4_out = COMP ? CARRY_t[12:10] : 3'bz;  // Controlled_Buffer controlled_buffer_4
  // Probe on CARRY_t[9:2]
  assign CARRY = ADD ? {CARRY_t[0], {7{1'b0}}} : 8'bz;  // Controlled_Buffer controlled_buffer_5
  assign CARRY = SUB ? {CARRY_t[1], {7{1'b0}}} : 8'bz;  // Controlled_Buffer controlled_buffer_6
  assign CARRY = MUL ? CARRY_t[9:2] : 8'bz;  // Controlled_Buffer controlled_buffer_7
  assign CARRY = controlled_buffer_4_out[0] ? 8'hc0 : 8'bz;  // Controlled_Buffer controlled_buffer_8
  assign CARRY = controlled_buffer_4_out[1] ? 8'h18 : 8'bz;  // Controlled_Buffer controlled_buffer_9
  assign CARRY = controlled_buffer_4_out[2] ? 8'h3 : 8'bz;  // Controlled_Buffer controlled_buffer_10
endmodule
