// Logisim project Addierer.circ as structural Verilog: 5 circuits, main circuit Main
module Halfadder (
  input  A,
  input  B,
  output S,
  output C
);

  wire and_1_out, and_2_out;

  and and_1 (and_1_out, A, ~B);  // AND_Gate
  and and_2 (and_2_out, ~A, B);  // AND_Gate
  and and_3 (C, A, B);
  or or_1 (S, and_1_out, and_2_out);
endmodule

module AdderSerial (
  input  [7:0] In,
  input  LD_A,
  input  LD_B,
  input  Shift_EN,
  input  CLK,
  output [7:0] Out
);

  wire d_ff_1_q, fulladder_1_c_out, fulladder_1_s, shift_register_2_out, shift_register_3_out;

  Shift_Register shift_register_1 (
    .shift(Shift_EN), .in(fulladder_1_c_out), .clk(CLK), .load(1'b0), .q0(Out[7]), .q1(Out[6]), .q2(Out[5]),
    .q3(Out[4]), .q4(Out[3]), .q5(Out[2]), .q6(Out[1]), .q7(Out[0]));  // open: out, clr, d0, d1, d2, d3, d4, d5, d6, d7
  Shift_Register shift_register_2 (
    .shift(Shift_EN), .clk(CLK), .out(shift_register_2_out), .load(LD_A), .d0(In[7]), .d1(In[6]), .d2(In[5]),
    .d3(In[4]), .d4(In[3]), .d5(In[2]), .d6(In[1]), .d7(In[0]));  // open: in, clr, q0, q1, q2, q3, q4, q5, q6, q7
  Shift_Register shift_register_3 (
    .shift(Shift_EN), .clk(CLK), .out(shift_register_3_out), .load(LD_B), .d0(In[7]), .d1(In[6]), .d2(In[5]),
    .d3(In[4]), .d4(In[3]), .d5(In[2]), .d6(In[1]), .d7(In[0]));  // open: in, clr, q0, q1, q2, q3, q4, q5, q6, q7
  Fulladder fulladder_1 (
    .A(shift_register_2_out), .B(shift_register_3_out), .C_in(d_ff_1_q), .C_out(fulladder_1_c_out),
    .S(fulladder_1_s));
  D_Flip_Flop d_ff_1 (.clk(CLK), .D(fulladder_1_s), .Q(d_ff_1_q));  // open: Qn, preset, en, reset
endmodule

module Fulladder (
  input  A,
  input  B,
  input  C_in,
  output C_out,
  output S
);

  wire halfadder_1_c, halfadder_1_s, halfadder_2_c;

  Halfadder halfadder_1 (.A(A), .B(B), .S(halfadder_1_s), .C(halfadder_1_c));
  Halfadder halfadder_2 (.A(halfadder_1_c), .B(C_in), .S(S), .C(halfadder_2_c));
  or or_1 (C_out, halfadder_1_s, halfadder_2_c);
endmodule

module Main (
  output [7:0] out_1,
  output [11:0] out_2
);

  wire button_1_out, clock_1_out;
  wire [7:0] counter_1_q;
  wire [11:0] rom_2_data;

  Button button_1 (.out(button_1_out));
  Clock clock_1 (.out(clock_1_out));
  Counter #(.max('h13)) counter_1 (
    .Q(counter_1_q), .clk(clock_1_out), .clr(button_1_out));  // open: load, D, count, carry
  ROM #(.dataWidth(12)) rom_1 (.addr(counter_1_q));  // open: data, sel
  ROM #(.dataWidth(12)) rom_2 (.addr(counter_1_q), .data(rom_2_data));  // open: sel
  // _12BitSwitcher 12bitswitcher_1: pin names not known; wires that end beside it: rom_2_data, out_2
  AdderSerial adderserial_1 (
    .LD_A(out_2[8]), .Out(out_1), .In(out_2[7:0]), .LD_B(out_2[9]), .CLK(out_2[11]));  // open: Shift_EN

  // Notes on the sheet:
  //   contents of rom_1 (hex, n*v repeats v):
  //   4*111 11 11 5*0 10 7 0 1 1 11 11 14*0 11 11 14*0 11 11
  //   contents of rom_2 (hex, n*v repeats v):
  //   69 68 75 74 3 2 3 2 3 2 3 2 3 2 3 2 3 2 3 2
endmodule

module _12BitSwitcher (
  input  [11:0] in_1,
  output [11:0] out_2
);


  assign out_2 = {in_1[0], in_1[1], in_1[2], in_1[3], in_1[4], in_1[5], in_1[6], in_1[7], in_1[8], in_1[9], in_1[10], in_1[11]};
endmodule
