// Logisim project Register_Read_and_Write.circ as structural Verilog
module TestVektor (
  input  [1:0] ADR,
  input  CS,
  input  [7:0] D,
  input  R,
  output [7:0] Q1
);

  wire comparator_1_eq, comparator_1_gt, comparator_1_lt, multiplexer_1_out, shift_register_1_p1,
       shift_register_1_p2, shift_register_1_p3, shift_register_1_p4, shift_register_1_p5,
       shift_register_1_p6, shift_register_1_p7, shift_register_1_p8, shift_register_1_p9,
       shift_register_1_p10;
  wire [7:0] counter_1_q, mcregister_1_q2;

  // Shift_Register shift_register_1: pin names not known; wires that end beside it: shift_register_1_p1, shift_register_1_p2, shift_register_1_p3, shift_register_1_p4, shift_register_1_p5, shift_register_1_p6, shift_register_1_p7, shift_register_1_p8, shift_register_1_p9, shift_register_1_p10
  Clock clock_1 (.out(shift_register_1_p1));
  MCRegister mcregister_1 (.ADR(ADR), .CS(CS), .D(D), .R(R), .Q1(Q1), .Q2(mcregister_1_q2));
  not not_1 (shift_register_1_p2, multiplexer_1_out);
  Multiplexer #(.select(3), .enable("false")) multiplexer_1 (
    .in0(shift_register_1_p3), .in1(shift_register_1_p4), .in2(shift_register_1_p5),
    .in3(shift_register_1_p6), .in4(shift_register_1_p7), .in5(shift_register_1_p8),
    .in6(shift_register_1_p9), .in7(shift_register_1_p10), .out(multiplexer_1_out),
    .sel({Q1[0], Q1[1], Q1[2]}));
  Counter counter_1 (.clk(multiplexer_1_out), .Q(counter_1_q));  // open: clr, load, up, count, D, carry
  // Probe on mcregister_1_q2
  Comparator comparator_1 (
    .a(mcregister_1_q2), .b(counter_1_q), .gt(comparator_1_gt), .eq(comparator_1_eq), .lt(comparator_1_lt));
  // Probe on counter_1_q
  // Probe on comparator_1_gt
  // Probe on comparator_1_eq
  // Probe on comparator_1_lt
endmodule

module MCRegister (
  input  [1:0] ADR,
  input  CS,
  input  [7:0] D,
  input  R,
  output [7:0] Q1,
  output [7:0] Q2
);

  wire decoder_1_out0, decoder_1_out1;

  Decoder #(.select(2)) decoder_1 (
    .out0(decoder_1_out0), .out1(decoder_1_out1), .sel(ADR), .en(CS));  // open: out2, out3
  Register register_1 (.D(D), .en(decoder_1_out0), .clk(R), .Q(Q1));  // open: clr
  Register register_2 (.D(D), .en(decoder_1_out1), .clk(R), .Q(Q2));  // open: clr
endmodule
