// Logisim project ioPort.circ as structural Verilog
module IOPort__Einzeln (
  input  in_1,
  input  in_2,
  input  PA0,
  input  in_4,
  input  in_5,
  input  in_6,
  input  in_7,
  input  in_8,
  input  in_9,
  output out_10
);

  wire d_ff_1_q, d_ff_2_q, d_ff_3_q, not_1_out, pull_resistor_1_node;

  Pull_Resistor #(.pull(1)) pull_resistor_1 (.node(pull_resistor_1_node));
  Transistor #(.gate("br")) transistor_1 (.in(PA0), .out(pull_resistor_1_node), .gate(not_1_out));
  not not_1 (not_1_out, in_1);
  assign PA0 = d_ff_2_q ? d_ff_3_q : 1'bz;  // Controlled_Buffer controlled_buffer_1
  D_Flip_Flop d_ff_1 (.clk(in_9), .D(PA0), .Q(d_ff_1_q));  // open: Qn, preset, en, reset
  D_Flip_Flop d_ff_2 (.clk(in_4), .D(out_10), .Q(d_ff_2_q), .reset(in_2));  // open: Qn, preset, en
  D_Flip_Flop d_ff_3 (.clk(in_7), .D(out_10), .Q(d_ff_3_q), .reset(in_2));  // open: Qn, preset, en
  assign out_10 = in_8 ? d_ff_1_q : 1'bz;  // Controlled_Buffer controlled_buffer_2
  assign out_10 = in_5 ? d_ff_2_q : 1'bz;  // Controlled_Buffer controlled_buffer_3
  assign out_10 = in_6 ? d_ff_3_q : 1'bz;  // Controlled_Buffer controlled_buffer_4
  // Probe on out_10

  // Other names for the same wires on the sheet: CLK = in_9; PUD = in_1; RDA0 = in_5; RESET = in_2; RPA0 = in_8;
  //   RRA0 = in_6; WDA0 = in_4; WRA0 = in_7

  // Notes on the sheet:
  //   Write Data
  //   Read Data
  //   Read 
  //   PINA0
  //   DDRA0
  //   PORTA0
endmodule

module PORT__Einzeln__Test (
  input  in_1,
  input  in_2,
  input  in_3
);

  wire button_1_out, clock_1_out, clock_2_out;
  wire [3:0] counter_1_q;
  wire [7:0] rom_1_data;

  Counter #(.width(4), .max('hf)) counter_1 (
    .Q(counter_1_q), .clk(clock_1_out), .clr(button_1_out));  // open: load, D, count, carry
  Clock clock_1 (.out(clock_1_out));
  Button button_1 (.out(button_1_out));
  // Probe on counter_1_q
  ROM #(.addrWidth(4)) rom_1 (.addr(counter_1_q), .data(rom_1_data));  // open: sel
  Clock clock_2 (.out(clock_2_out));
  IOPort__Einzeln ioport_einzeln_1 (
    .in_1(in_1), .in_2(rom_1_data[5]), .PA0(in_2), .in_4(rom_1_data[4]), .in_5(rom_1_data[3]),
    .in_6(rom_1_data[2]), .in_7(rom_1_data[1]), .in_9(clock_2_out), .in_8(rom_1_data[0]), .out_10(in_3));
  // Probe on in_3

  // Notes on the sheet:
  //   DDR=0: INPUT
  //   DDR=1: OUTPUT
  //   contents of rom_1 (hex, n*v repeats v):
  //   20 10 1 0 3 0 4 0 5 0 6 0 7 0 8
endmodule

// PIO
module MPIO (
  input  [7:0] in_1,
  input  PUD,
  input  Reset,
  input  WDA0,
  input  RDA0,
  input  RRA0,
  input  WRA0,
  input  RPA0,
  input  CLK,
  output [7:0] out_10
);

  IOPort__Einzeln ioport_einzeln_1 (
    .in_1(PUD), .in_2(Reset), .PA0(in_1[0]), .in_4(WDA0), .in_5(RDA0), .in_6(RDA0), .in_7(WRA0), .in_9(CLK),
    .in_8(RPA0), .out_10(out_10[0]));
  IOPort__Einzeln ioport_einzeln_2 (
    .in_1(PUD), .in_2(Reset), .PA0(in_1[1]), .in_4(WDA0), .in_5(RDA0), .in_6(RDA0), .in_7(WRA0), .in_9(CLK),
    .in_8(RPA0), .out_10(out_10[1]));
  IOPort__Einzeln ioport_einzeln_3 (
    .in_1(PUD), .in_2(Reset), .PA0(in_1[2]), .in_4(WDA0), .in_5(RDA0), .in_6(RDA0), .in_7(WRA0), .in_9(CLK),
    .in_8(RPA0), .out_10(out_10[2]));
  IOPort__Einzeln ioport_einzeln_4 (
    .in_1(PUD), .in_2(Reset), .PA0(in_1[3]), .in_4(WDA0), .in_5(RDA0), .in_6(RDA0), .in_7(WRA0), .in_9(CLK),
    .in_8(RPA0), .out_10(out_10[3]));
  IOPort__Einzeln ioport_einzeln_5 (
    .in_1(PUD), .in_2(Reset), .PA0(in_1[4]), .in_4(WDA0), .in_5(RDA0), .in_6(RDA0), .in_7(WRA0), .in_9(CLK),
    .in_8(RPA0), .out_10(out_10[4]));
  IOPort__Einzeln ioport_einzeln_6 (
    .in_1(PUD), .in_2(Reset), .PA0(in_1[5]), .in_4(WDA0), .in_5(RDA0), .in_6(RDA0), .in_7(WRA0), .in_9(CLK),
    .in_8(RPA0), .out_10(out_10[5]));
  IOPort__Einzeln ioport_einzeln_7 (
    .in_1(PUD), .in_2(Reset), .PA0(in_1[6]), .in_4(WDA0), .in_5(RDA0), .in_6(RDA0), .in_7(WRA0), .in_9(CLK),
    .in_8(RPA0), .out_10(out_10[6]));
  IOPort__Einzeln ioport_einzeln_8 (
    .in_1(PUD), .in_2(Reset), .PA0(in_1[7]), .in_4(WDA0), .in_5(RDA0), .in_6(RDA0), .in_7(WRA0), .in_9(CLK),
    .in_8(RPA0), .out_10(out_10[7]));

  assign RRA0 = RDA0;
endmodule

module PORT__8_Bit (
  input  R_W,
  input  RESET,
  input  CLK,
  input  CS,
  input  [1:0] ADDR,
  input  [7:0] PIO,
  output [7:0] out_7
);

  wire and_out;

  and \and  (and_out, CLK, CS);
  Demultiplexer #(.select(2), .enable("false")) demultiplexer_1 (
    .in(1'b1), .sel(ADDR));  // open: out0, out1, out2, out3
  MPIO mpio_1 (.Reset(RESET), .CLK(and_out), .in_1(PIO), .out_10(out_7));  // open: PUD, WDA0, RDA0, RRA0, WRA0, RPA0
endmodule

module MCIO (
  input  RESET,
  input  CLK,
  input  R_W,
  input  [3:0] ADDR,
  input  CS,
  input  [7:0] PORTA,
  input  [7:0] PORTB,
  input  [7:0] PORTC,
  output [7:0] DATABUS
);

  wire and_2_out, and_3_out, and_out, decoder_1_out0, decoder_1_out1, decoder_1_out2;

  Decoder #(.select(2)) decoder_1 (
    .out0(decoder_1_out0), .out1(decoder_1_out1), .out2(decoder_1_out2), .sel(ADDR[3:2]));  // open: out3, en
  and \and  (and_out, decoder_1_out0, CS);
  and and_2 (and_2_out, decoder_1_out1, CS);
  and and_3 (and_3_out, decoder_1_out2, CS);
  PORT__8_Bit port_8_bit_1 (
    .R_W(R_W), .RESET(RESET), .CLK(CLK), .CS(and_out), .ADDR(ADDR[1:0]), .PIO(PORTA), .out_7(DATABUS));
  PORT__8_Bit port_8_bit_2 (
    .R_W(R_W), .RESET(RESET), .CLK(CLK), .CS(and_2_out), .ADDR(ADDR[1:0]), .PIO(PORTB), .out_7(DATABUS));
  PORT__8_Bit port_8_bit_3 (
    .R_W(R_W), .RESET(RESET), .CLK(CLK), .CS(and_3_out), .ADDR(ADDR[1:0]), .PIO(PORTC), .out_7(DATABUS));

  // Notes on the sheet:
  //   PORTA
  //   PORTB
  //   PORTC
endmodule
